// Digital circuit 1-bit-adder.dig as structural Verilog
module _1_bit_adder (
  input  A,
  input  B,
  input  Carry_In,
  output Sum,
  output Carry_Out
);

  wire and_1_out, and_2_out, xor_1_out;

  xor xor_1 (xor_1_out, A, B);
  xor xor_2 (Sum, xor_1_out, Carry_In);
  and and_1 (and_1_out, xor_1_out, Carry_In);
  and and_2 (and_2_out, A, B);
  or or_1 (Carry_Out, and_1_out, and_2_out);
endmodule
