// Digital circuit 2-bit-multiplier.dig as structural Verilog
module _2_bit_multiplier (
  input  [1:0] A,
  input  [1:0] B,
  output [3:0] Output
);

  wire and_1_out, and_2_out, and_3_out, and_4_out, and_5_out, and_6_out;

  and and_1 (and_1_out, ~A[1], A[0], B[1]);  // And
  and and_2 (and_2_out, A[0], B[1], ~B[0]);  // And
  and and_3 (and_3_out, A[1], ~B[1], B[0]);  // And
  and and_4 (and_4_out, A[1], ~A[0], B[0]);  // And
  and and_5 (and_5_out, A[1], ~A[0], B[1]);  // And
  and and_6 (and_6_out, A[1], B[1], ~B[0]);  // And
  and and_7 (Output[3], A[1], A[0], B[1], B[0]);
  and and_8 (Output[0], A[0], B[0]);
  or or_1 (Output[1], and_1_out, and_2_out, and_3_out, and_4_out);
  or or_2 (Output[2], and_5_out, and_6_out);

  // Notes on the sheet:
  //   P_3
  //   P_1
  //   P_2
  //   P_0
endmodule
