// Digital circuit 4-bit-adder.dig as structural Verilog
module _4_bit_adder (
  input  [3:0] A,
  input  [3:0] B,
  output Overflow_Bit___Flag,
  output [3:0] Output
);

  wire _1_bit_adder_2_carry_out, _1_bit_adder_3_carry_out, _1_bit_adder_4_carry_out;

  _1_bit_adder _1_bit_adder_1 (
    .A(A[3]), .B(B[3]), .Carry_In(_1_bit_adder_2_carry_out), .Sum(Output[3]), .Carry_Out(Overflow_Bit___Flag));
  _1_bit_adder _1_bit_adder_2 (
    .A(A[2]), .B(B[2]), .Carry_In(_1_bit_adder_3_carry_out), .Sum(Output[2]),
    .Carry_Out(_1_bit_adder_2_carry_out));
  _1_bit_adder _1_bit_adder_3 (
    .A(A[1]), .B(B[1]), .Carry_In(_1_bit_adder_4_carry_out), .Sum(Output[1]),
    .Carry_Out(_1_bit_adder_3_carry_out));
  _1_bit_adder _1_bit_adder_4 (
    .A(A[0]), .B(B[0]), .Carry_In(1'b0), .Sum(Output[0]), .Carry_Out(_1_bit_adder_4_carry_out));
endmodule
